// Logisim project Lock.circ as structural Verilog
module EDGE_DETECT (
  input  BTN,
  input  CLK,
  output EV,
  output PREV
);

  wire not_1_out;

  D_Flip_Flop d_ff_1 (.D(BTN), .clk(CLK), .Q(PREV));  // open: Qn, preset, reset
  not not_1 (not_1_out, PREV);
  and and_1 (EV, BTN, not_1_out);

  // Notes on the sheet:
  //   PREV: Previous button value
  //   EV: Detect if a button is activated which was previously not
endmodule

module EVENT_LOGIC (
  input  RUN,
  input  RESET,
  input  S1,
  input  S0,
  input  CLR_EV,
  input  ENT_EV,
  input  [3:0] DIGIT,
  output EN,
  output IN_ENTRY,
  output IN_UNL,
  output DO_CLEAR,
  output VALID_ENT,
  output INV_ENT
);

  wire DO_ENTER, INV, or_1_out;

  and and_1 (EN, RUN, ~RESET);  // AND_Gate
  or or_1 (or_1_out, DIGIT[1], DIGIT[2]);
  nor nor_1 (IN_ENTRY, S1, S0);
  and and_2 (IN_UNL, ~S1, S0);  // AND_Gate
  and and_3 (INV, or_1_out, DIGIT[3]);
  and and_4 (DO_CLEAR, EN, IN_ENTRY, CLR_EV);
  and and_5 (DO_ENTER, EN, ~CLR_EV, ENT_EV, IN_ENTRY);  // AND_Gate
  and and_6 (VALID_ENT, DO_ENTER, ~INV);  // AND_Gate
  and and_7 (INV_ENT, DO_ENTER, INV);

  // Notes on the sheet:
  //   S : 00 :  IN ENTRY
  //   01 : UNCLOCKED
  //   10 : LOCKED
  //   CLR_EV : Clear Event
  //   ENT_EV : Enter Event
  //   EN : Running and not Reset
  //   DO_CLEAR : Clear event and in entry
  //   INV : Invalid digits (10-15)
  //   VALID_ENT : Valid entry
  //   INV_ENT : Invalid Entry
  //   DO_ENTER : Enter event and in entry
endmodule
